# Fritzing sketch 24v analog signal (saved by Fritzing 0.9.3b)
breadboards: 1

parts:
  PSU1 = Adjustable Breadboard Power Supply  # not connected
  J1 = STM32 Nucleo boards  # not connected
  J3 = screw terminal, 3 pins
  R1 = Resistor [tolerance=±5% resistance=100 package="0805 [SMD]"]
  J4 = Screw terminal - 2 pins [package=THT]

nets:
  N1: J3.pin1, R1.Pin_0, J4.pin1
  N2: J3.pin2, J3.pin3, R1.Pin_1, J4.pin2
