# Fritzing sketch TempSensorRTD2020-03-03 (saved by Fritzing 0.9.3b)
circuit board: 4.9741cm x 5.56661cm
breadboards: 1

parts:
  U1 = OP37 - Low Noise, Precision, High Speed Op Amp [part_number=OP37]
  R1 = Resistor [tolerance=±5% resistance=3.3k package=THT]
  R2 = Resistor [tolerance=±5% resistance=3.3k package=THT]
  R3 = Resistor [tolerance=±5% resistance=100 package=THT]
  RTD = Header 2 [package=screwterminal-3.5mm-2_lock]
  R4 = Resistor [tolerance=±5% resistance=3.3k package=THT]
  R5 = Resistor [tolerance=±5% resistance=3.3k package=THT]
  V- = Header 1 [package=1x01_offset]
  V+ = Header 2 [package=screwterminal-3.5mm-2_lock]
  Out = Header 1 [package=1x01_offset]

nets:
  N1: U1.-IN, R1.Pin_1, RTD.2, R4.Pin_0
  N2: U1.+IN, R2.Pin_1, R3.Pin_0, R5.Pin_0
  N3: U1.-V, V-.1
  N4: U1.OUT, R1.Pin_0, Out.1
  N5: U1.V+, R4.Pin_1, R5.Pin_1, V+.2
  N6: R2.Pin_0, R3.Pin_1, RTD.1, V+.1

notes:
  V+
  Output
  V-
  RTD
  V+/gnd
  GND
  100
  3.3k
  Nuc
  OpA
  Adrian DB
