# Fritzing sketch Tempsensor RTDpt100 (saved by Fritzing 0.9.3b)
circuit board: 8.46667cm x 5.64444cm
breadboards: 1

parts:
  U1 = OP37 - Low Noise, Precision, High Speed Op Amp [part_number=OP37]
  R1 = Resistor [tolerance=±5% resistance=220 package=THT]
  R2 = Resistor [tolerance=±5% resistance=220 package=THT]
  R3 = Resistor [tolerance=±5% resistance=220 package=THT]
  RTD = Header 2 [package=screwterminal-3.5mm-2_lock]
  R4 = Resistor [tolerance=±5% resistance=220 package=THT]
  R5 = Resistor [tolerance=±5% resistance=220 package=THT]
  Vin = Header 2 [package=screwterminal-3.5mm-2_lock]

nets:
  N1: U1.-IN, R1.Pin_1, RTD.2, R4.Pin_0
  N2: U1.+IN, R2.Pin_1, R3.Pin_0, R5.Pin_0
  N3: U1.OUT, R1.Pin_0
  N4: R2.Pin_0, R3.Pin_1, RTD.1, Vin.1
  N5: R4.Pin_1, R5.Pin_1, Vin.2
