# Fritzing sketch circuit for analog signal (saved by Fritzing 0.9.3b)
breadboards: 1

parts:
  R1 = Resistor [tolerance=±5% resistance=100 package=THT]
  R2 = Resistor [tolerance=±5% resistance=3.3k package=THT]
  R3 = Resistor [tolerance=±5% resistance=3.3k package=THT]
  R4 = Resistor [tolerance=±5% resistance=100 package=THT]
  U1 = LM124-324 Quad Opamp [package="DIP (Dual Inline)"]
  3_3v = Battery Holders [package=battery-aa]
  R5 = Resistor [tolerance=±5% resistance=3.3k package=THT]
  R6 = Resistor [tolerance=±5% resistance=3.3k package=THT]
  R7 = Resistor [tolerance=±5% resistance=3.3k package=THT]
  R8 = Resistor [tolerance=±5% resistance=3.3k package=THT]
  3_3v1 = Battery Holders [package=battery-aa]
  IC1 = Dual Op-Amp [package=so08]
  R9 = Resistor [tolerance=±5% resistance=3.3k package=THT]
  R10 = Resistor [tolerance=±5% resistance=3.3k package=THT]
  R11 = Resistor [tolerance=±5% resistance=100 package=THT]
  R12 = Resistor [tolerance=±5% resistance=100 package=THT]
  R13 = Resistor [tolerance=±5% resistance=3.3k package=THT]
  R14 = Resistor [tolerance=±5% resistance=3.3k package=THT]

nets:
  N1: R1.Pin_0, R2.Pin_1, U1.1IN+
  N2: R1.Pin_1, R4.Pin_1, U1.VCC+, 3_3v.+
  N3: R2.Pin_0, R3.Pin_0, U1.VCC-, 3_3v.-
  N4: R3.Pin_1, R4.Pin_0, U1.2IN+
  N5: U1.1OUT, U1.1IN-, R5.Pin_0
  N6: U1.2IN-, U1.2OUT, R8.Pin_0
  N7: U1.3OUT, R6.Pin_1
  N8: U1.3IN-, R5.Pin_1, R6.Pin_0
  N9: U1.3IN+, R7.Pin_0, R8.Pin_1
  GND: R7.Pin_1, R14.Pin_0
  N10: 3_3v1.-, R11.Pin_0, R12.Pin_0
  N11: 3_3v1.+, R9.Pin_1, R10.Pin_1
  N12: IC1.B_+IN, R9.Pin_0, R11.Pin_1, R14.Pin_1
  N13: IC1.B_-IN, R10.Pin_0, R12.Pin_1, R13.Pin_0
  N14: IC1.B_OUT, R13.Pin_1
